// Logisim project SIMULATION_AND_IMPLEMENTATION_IC.circ as structural Verilog: 1 circuit, main circuit main
module main (
);

  wire A_p1, n7447_1_pin8, n7447_1_pin9, n7447_1_pin10, n7447_1_pin11, n7447_1_pin12, n7447_1_pin13,
       n7447_1_pin14, n7447_1_pin15, n7447_2_pin9, n7447_2_pin10, n7447_2_pin11, n7447_2_pin12,
       n7447_2_pin13, n7447_2_pin14, n7447_2_pin15, n7447_3_pin9, n7447_3_pin10, n7447_3_pin11,
       n7447_3_pin12, n7447_3_pin13, n7447_3_pin14, n7447_3_pin15, n7486_1_pin3, n7486_1_pin6, n7486_1_pin8,
       n7486_1_pin11, n74283_1_pin1, n74283_1_pin4, n74283_1_pin10, n74283_1_pin13, pull_resistor_1_node,
       pull_resistor_2_node, pull_resistor_3_node, pull_resistor_4_node, pull_resistor_5_node,
       pull_resistor_6_node, pull_resistor_7_node, pull_resistor_8_node, R_p2;

  Pull_Resistor pull_resistor_1 (.node(pull_resistor_1_node));
  // Switch A: pin names not known; wires that end beside it: A_p1, pull_resistor_1_node
  Pull_Resistor pull_resistor_2 (.node(pull_resistor_2_node));
  // Switch switch_1: pin names not known; wires that end beside it: A_p1, pull_resistor_2_node
  Pull_Resistor pull_resistor_3 (.node(pull_resistor_3_node));
  // Switch switch_2: pin names not known; wires that end beside it: A_p1, pull_resistor_3_node
  Pull_Resistor pull_resistor_4 (.node(pull_resistor_4_node));
  // Switch switch_3: pin names not known; wires that end beside it: A_p1, pull_resistor_4_node
  Pull_Resistor pull_resistor_5 (.node(pull_resistor_5_node));
  // Switch B: pin names not known; wires that end beside it: A_p1, pull_resistor_5_node
  Pull_Resistor pull_resistor_6 (.node(pull_resistor_6_node));
  // Switch switch_4: pin names not known; wires that end beside it: A_p1, pull_resistor_6_node
  Pull_Resistor pull_resistor_7 (.node(pull_resistor_7_node));
  // Switch switch_5: pin names not known; wires that end beside it: A_p1, pull_resistor_7_node
  Pull_Resistor pull_resistor_8 (.node(pull_resistor_8_node));
  // Switch switch_6: pin names not known; wires that end beside it: A_p1, pull_resistor_8_node
  // Switch R: pin names not known; wires that end beside it: A_p1, R_p2
  _7486 #(.ShowInternalStructure("true")) u_7486_1 (
    .pin1(pull_resistor_5_node), .pin2(R_p2), .pin3(n7486_1_pin3), .pin4(pull_resistor_7_node), .pin5(R_p2),
    .pin6(n7486_1_pin6), .pin13(pull_resistor_6_node), .pin12(R_p2), .pin11(n7486_1_pin11),
    .pin10(pull_resistor_8_node), .pin9(R_p2), .pin8(n7486_1_pin8));
  Pull_Resistor pull_resistor_9 (.node(R_p2));
  _74283 #(.ShowInternalStructure("true")) u_74283_1 (
    .pin1(n74283_1_pin1), .pin2(n7486_1_pin11), .pin3(pull_resistor_2_node), .pin4(n74283_1_pin4),
    .pin5(pull_resistor_1_node), .pin6(n7486_1_pin3), .pin7(R_p2), .pin15(n7486_1_pin6),
    .pin14(pull_resistor_3_node), .pin13(n74283_1_pin13), .pin12(pull_resistor_4_node), .pin11(n7486_1_pin8),
    .pin10(n74283_1_pin10));  // open: pin9
  _7447 #(.ShowInternalStructure("true"), .VccGndPorts("true")) u_7447_1 (
    .pin1(pull_resistor_6_node), .pin2(pull_resistor_7_node), .pin6(pull_resistor_8_node),
    .pin7(pull_resistor_5_node), .pin8(n7447_1_pin8), .pin16(A_p1), .pin15(n7447_1_pin15),
    .pin14(n7447_1_pin14), .pin13(n7447_1_pin13), .pin12(n7447_1_pin12), .pin11(n7447_1_pin11),
    .pin10(n7447_1_pin10), .pin9(n7447_1_pin9));  // open: pin3, pin4, pin5
  _7_Segment_Display #(.active("false")) u_7_segment_display_1 (
    .g(n7447_1_pin14), .f(n7447_1_pin15), .a(n7447_1_pin13), .b(n7447_1_pin12), .e(n7447_1_pin9),
    .d(n7447_1_pin10), .c(n7447_1_pin11));  // open: dp
  _7447 #(.ShowInternalStructure("true"), .VccGndPorts("true")) u_7447_2 (
    .pin1(n74283_1_pin1), .pin2(n74283_1_pin13), .pin6(n74283_1_pin10), .pin7(n74283_1_pin4),
    .pin8(n7447_1_pin8), .pin16(A_p1), .pin15(n7447_2_pin15), .pin14(n7447_2_pin14), .pin13(n7447_2_pin13),
    .pin12(n7447_2_pin12), .pin11(n7447_2_pin11), .pin10(n7447_2_pin10), .pin9(n7447_2_pin9));  // open: pin3, pin4, pin5
  _7_Segment_Display #(.active("false")) u_7_segment_display_2 (
    .g(n7447_2_pin14), .f(n7447_2_pin15), .a(n7447_2_pin13), .b(n7447_2_pin12), .e(n7447_2_pin9),
    .d(n7447_2_pin10), .c(n7447_2_pin11));  // open: dp
  _7447 #(.ShowInternalStructure("true"), .VccGndPorts("true")) u_7447_3 (
    .pin1(pull_resistor_2_node), .pin2(pull_resistor_3_node), .pin6(pull_resistor_4_node),
    .pin7(pull_resistor_1_node), .pin8(n7447_1_pin8), .pin16(A_p1), .pin15(n7447_3_pin15),
    .pin14(n7447_3_pin14), .pin13(n7447_3_pin13), .pin12(n7447_3_pin12), .pin11(n7447_3_pin11),
    .pin10(n7447_3_pin10), .pin9(n7447_3_pin9));  // open: pin3, pin4, pin5
  _7_Segment_Display #(.active("false")) u_7_segment_display_3 (
    .g(n7447_3_pin14), .f(n7447_3_pin15), .a(n7447_3_pin13), .b(n7447_3_pin12), .e(n7447_3_pin9),
    .d(n7447_3_pin10), .c(n7447_3_pin11));  // open: dp
  // also tied to GND on the sheet: n7447_1_pin8
  // also tied to VCC on the sheet: A_p1

  // Notes on the sheet:
  //   B
  //   A  - / +  B
  //   A
endmodule
